# Fritzing sketch NanoFanController (saved by Fritzing 0.9.4)
breadboards: 1

parts:
  Arduino = Arduino Nano (Rev3.0) (ICSP)
  R1 = Resistor [tolerance=±5% resistance=2.2k package=THT]
  R2 = Temperature Sensor (Thermistor) [thermistor_type=NTC part_number=10k package=THT]
  D1 = Diode [part_number=1N4007 package=diode-1n4001]
  U1 = mystery part, 4 pins [chip_label="Mobo connector"]
  Fan_3 = mystery part, 4 pins [chip_label="Noctua fan"]
  Fan_1 = mystery part, 4 pins [chip_label="Noctua fan"]
  Fan_2 = mystery part, 4 pins [chip_label="Noctua fan"]

nets:
  N1: Arduino.GND, R1.Pin_1, U1.pin4
  N2: Arduino.D3, Fan_3.pin1
  N3: Arduino.D9, Fan_1.pin1
  N4: Arduino.D10, Fan_2.pin1
  N5: Arduino.VIN, D1.C
  N6: Arduino.5V, R2.pin_1
  N7: Arduino.A7, R1.Pin_0, R2.pin_0
  N8: D1.A, U1.pin3
  N9: Fan_3.pin3, Fan_1.pin3, Fan_2.pin3
  N10: Fan_3.pin4, Fan_1.pin4, Fan_2.pin4
